# Fritzing sketch Schematic (saved by Fritzing 0.9.10b)

parts:
  L298N1 = L298N DC motor driver
  L298N2 = L298N DC motor driver
  Mod1 = Amica NodeMCU DEVKIT 1.0
  M1 = gear-motor
  M2 = gear-motor
  M3 = gear-motor  # not connected
  M4 = gear-motor
  U1 = LIPO-1000mAh [package=lipo-1000]
  J1 = Piezo Speaker

nets:
  N1: L298N1.OUT1, M4.pin_2
  N2: L298N1.OUT2, M4.pin_1
  N3: L298N1.GND, J1.pin1
  N4: L298N1.IN1, Mod1.pin_14
  N5: L298N1.IN2, Mod1.pin5
  N6: L298N1.IN3, Mod1.pin_11
  N7: L298N1.IN4, Mod1.pin8
  N8: L298N2.OUT1, M2.pin_2
  N9: L298N2.OUT2, M2.pin_1
  N10: L298N2.OUT3, M1.pin_2
  N11: L298N2.OUT4, M1.pin_1
  N12: L298N2.IN1, Mod1.pin3
  N13: L298N2.IN2, Mod1.pin4
  N14: L298N2.IN3, Mod1.pin2, Mod1.pin_9, Mod1.pin_25, U1.-
  N15: L298N2.IN4, Mod1.pin_10, Mod1.pin_26
  N16: Mod1.pin_15, J1.pin2

custom parts:
  L298N DC motor driver: 2x DC motor driver with 78M05 positive voltage regulator (7..35 V) L298N: max 46 V, 2 A Set 5 V Enable jumper to enable 5 V regultor (needed for the L298N) and +5 V output at screw terminal or supply external +5 V at screw terminal Set ENA and/or ENB to +5 V to enable motor permanently or supply ENA and/or ENB with PWM signal IN1 and IN2 set rotation directory for motor A (OUT1/OUT2) IN2 and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
